# Fritzing sketch PythagoraPlayer (saved by Fritzing 0.9.2b)
circuit board: 8.46667cm x 5.64444cm
breadboards: 1

parts:
  R1 = Resistor [tolerance=±5% resistance=220 package=THT]
  S1 = Round Pushbutton
  J1 = Piezo Speaker
  パーツ1 = Arduino Uno (Rev3)

nets:
  N1: R1.Pin_0, J1.pin1, パーツ1.GND
  N2: R1.Pin_1, S1.leg0, パーツ1.D2
  N3: J1.pin2, パーツ1.D12/MISO

// code stored in the sketch: PythagoraPlayer.ino

